// Logisim project Exercicios.circ as structural Verilog: 1 circuit, main circuit main
module main (
  input  A,
  input  B,
  input  in_3,
  input  A_2,
  input  B_2,
  input  in_6,
  input  in_7,
  input  in_8,
  input  in_9,
  input  in_10,
  input  R_W,
  input  SELL,
  output out_13,
  output out_14,
  output out_15,
  output out_16,
  output out_17
);

  wire clock_1_out, d_ff_1_q, j_k_ff_1_q, j_k_ff_2_q, j_k_ff_3_q, nand_1_out, nand_2_out, nand_3_out,
       nand_4_out, nand_5_out, nand_6_out, not_1_out, not_2_out, not_3_out, not_4_out, not_5_out, not_6_out,
       not_7_out, not_8_out, or_1_out, or_2_out, undriven, undriven_2;

  not not_1 (not_1_out, R_W);
  nand nand_1 (nand_1_out, not_1_out, SELL);
  nand nand_2 (nand_2_out, SELL, R_W);
  assign nand_1_out = undriven ? ~not_2_out : 1'bz;  // Controlled_Inverter controlled_inverter_1
  not not_2 (not_2_out, out_17);
  Clock clock_1 (.out(clock_1_out));
  not not_3 (not_3_out, in_8);
  not not_4 (not_4_out, clock_1_out);
  assign nand_1_out = undriven_2 ? ~out_17 : 1'bz;  // Controlled_Inverter controlled_inverter_2
  nand nand_3 (nand_3_out, in_8, in_7);
  nand nand_4 (nand_4_out, in_7, not_3_out);
  J_K_Flip_Flop j_k_ff_1 (.J(in_9), .clk(not_4_out), .K(in_10), .Q(j_k_ff_1_q));  // open: Qn, preset, en, reset
  not not_5 (not_5_out, A);
  or or_1 (or_1_out, B_2, in_6);
  J_K_Flip_Flop j_k_ff_2 (.clk(not_6_out), .Q(j_k_ff_2_q));  // open: J, K, Qn, preset, en, reset
  not not_6 (not_6_out, j_k_ff_1_q);
  nand nand_5 (nand_5_out, undriven, nand_6_out);
  nand nand_6 (nand_6_out, nand_5_out, undriven_2);
  or or_2 (or_2_out, B, in_3);
  D_Flip_Flop d_ff_1 (.clk(A_2), .D(B_2), .Q(d_ff_1_q));  // open: Qn, preset, en, reset
  and and_1 (out_14, d_ff_1_q, or_1_out);
  nand nand_7 (out_15, nand_3_out, out_16);
  nand nand_8 (out_16, out_15, nand_4_out);
  not not_7 (not_7_out, j_k_ff_2_q);
  assign nand_2_out = out_17 ? ~nand_5_out : 1'bz;  // Controlled_Inverter controlled_inverter_3
  and and_2 (out_13, not_5_out, or_2_out);
  not not_8 (not_8_out, j_k_ff_3_q);
  J_K_Flip_Flop j_k_ff_3 (.clk(not_7_out), .Q(j_k_ff_3_q));  // open: J, K, Qn, preset, en, reset
  J_K_Flip_Flop j_k_ff_4 (.clk(not_8_out));  // open: J, K, Q, Qn, preset, en, reset

  // Notes on the sheet:
  //   Entrada
  //   Controle
  //   RAM
  //   Circuito Combinacional
  //   Circuito Sequencial
  //   Flip Flop Tipo D
  //   D
endmodule
